# Fritzing sketch ammeter-how-to (saved by Fritzing 0.8.7b)
breadboards: 1

parts:
  R2 = Resistor [tolerance=±5% resistance=1k package=THT]
  VCC1 = 4 x AAA Battery Mount
  Ammeter1 = Amperemeter

nets:
  N1: R2.Pin_0, VCC1.+
  N2: R2.Pin_1, Ammeter1.Positive
  N3: VCC1.-, Ammeter1.Com

custom parts:
  Amperemeter: A Standard Multimeter in Current mode
