# Fritzing sketch breadboard (saved by Fritzing 0.8.7b)
breadboards: 1

parts:
  Part1 = Arduino Pro Mini v13
  S1 = Pushbutton [package="[THT]"]

nets:
  N1: Part1.GND, S1.Pin_3, S1.Pin_4
  N2: Part1.RESET, S1.Pin_1, S1.Pin_2
