# Fritzing sketch ohmmeter-how-to (saved by Fritzing 0.8.7b)
breadboards: 1

parts:
  R2 = Resistor [tolerance=±5% resistance=1k package=THT]
  Ohmmeter1 = Ohmmeter

nets:
  N1: R2.Pin_0, Ohmmeter1.Positive
  N2: R2.Pin_1, Ohmmeter1.Com

custom parts:
  Ohmmeter: A Standard Multimeter in Current mode
