# Fritzing sketch voltmeter-how-to (saved by Fritzing 0.8.7b)
breadboards: 1

parts:
  R2 = Resistor [tolerance=±5% resistance=1k package=THT]
  VCC1 = 4 x AAA Battery Mount
  Voltmeter1 = Voltmeter

nets:
  N1: R2.Pin_0, VCC1.+, Voltmeter1.Positive
  N2: R2.Pin_1, VCC1.-, Voltmeter1.Com

custom parts:
  Voltmeter: A Standard Multimeter in Current mode
