# Fritzing sketch hb_1 (saved by Fritzing 0.8.7b)
breadboards: 1

parts:
  M1 = DC Motor
  D1 = Rectifier Diode [part_number=1N4001 package="300 mil [THT]"]
  S1 = Pushbutton [package="[THT]"]
  R1 = Resistor [tolerance=±5% resistance=330 package=THT]
  Q1 = PNP-Transistor [part_number=2N3906 package="TO92 [THT]"]

nets:
  GND: M1.pin_1, S1.Pin_3, S1.Pin_4
  N1: M1.pin_2, D1.anode, Q1.C
  5V: D1.cathode, Q1.E
  N2: S1.Pin_1, S1.Pin_2, R1.Pin_0
  N3: R1.Pin_1, Q1.B
