# Fritzing sketch hb_1_modified (saved by Fritzing 0.8.7b)
breadboards: 1

parts:
  M1 = DC Motor
  D1 = Rectifier Diode [part_number=1N4001 package="300 mil [THT]"]
  R1 = Resistor [tolerance=±5% resistance=330 package=THT]
  Q1 = PNP-Transistor [part_number=2N3906 package="TO92 [THT]"]
  Q2 = NPN-Transistor [part_number=2N3904 package="TO92 [THT]"]
  S1 = Pushbutton [package="[THT]"]
  R2 = Resistor [tolerance=±5% resistance=10k package=THT]

nets:
  GND: M1.pin_1, Q2.E
  N1: M1.pin_2, D1.anode, Q1.C
  5V: D1.cathode, Q1.E, S1.Pin_3, S1.Pin_4
  N2: R1.Pin_0, Q2.C
  N3: R1.Pin_1, Q1.B
  N4: Q2.B, R2.Pin_1
  N5: S1.Pin_1, S1.Pin_2, R2.Pin_0
