# Fritzing sketch hb_2 (saved by Fritzing 0.8.7b)
breadboards: 1

parts:
  M1 = DC Motor
  D1 = Rectifier Diode [part_number=1N4001 package="300 mil [THT]"]
  D4 = Rectifier Diode [part_number=1N4001 package="300 mil [THT]"]
  Q4 = NPN-Transistor [part_number=2N3904 package="TO92 [THT]"]
  S1 = Pushbutton [package="[THT]"]
  R1 = Resistor [tolerance=±5% resistance=330 package=THT]
  R4 = Resistor [tolerance=±5% resistance=330 package=THT]
  S4 = Pushbutton [package="[THT]"]
  Q1 = PNP-Transistor [part_number=2N3906 package="TO92 [THT]"]

nets:
  N1: M1.pin_1, D4.cathode, Q4.C
  N2: M1.pin_2, D1.anode, Q1.C
  5V: D1.cathode, S4.Pin_1, S4.Pin_2, Q1.E
  GND: D4.anode, Q4.E, S1.Pin_3, S1.Pin_4
  N3: Q4.B, R4.Pin_0
  N4: S1.Pin_1, S1.Pin_2, R1.Pin_0
  N5: R1.Pin_1, Q1.B
  N6: R4.Pin_1, S4.Pin_3, S4.Pin_4
