# Fritzing sketch hb_final (saved by Fritzing 0.8.7b)
breadboards: 1

parts:
  M1 = DC Motor
  D1 = Rectifier Diode [part_number=1N4001 package="300 mil [THT]"]
  D2 = Rectifier Diode [part_number=1N4001 package="300 mil [THT]"]
  D3 = Rectifier Diode [part_number=1N4001 package="300 mil [THT]"]
  D4 = Rectifier Diode [part_number=1N4001 package="300 mil [THT]"]
  Q2 = NPN-Transistor [part_number=2N3904 package="TO92 [THT]"]
  Q4 = NPN-Transistor [part_number=2N3904 package="TO92 [THT]"]
  S1 = Pushbutton [package="[THT]"]
  S2 = Pushbutton [package="[THT]"]
  R1 = Resistor [tolerance=±5% resistance=330 package=THT]
  R2 = Resistor [tolerance=±5% resistance=330 package=THT]
  R3 = Resistor [tolerance=±5% resistance=330 package=THT]
  R4 = Resistor [tolerance=±5% resistance=330 package=THT]
  Q1 = PNP-Transistor [part_number=2N3906 package="TO92 [THT]"]
  Q3 = PNP-Transistor [part_number=2N3906 package="TO92 [THT]"]
  Q5 = NPN-Transistor [part_number=2N3904 package="TO92 [THT]"]
  R5 = Resistor [tolerance=±5% resistance=10k package=THT]
  Q6 = NPN-Transistor [part_number=2N3904 package="TO92 [THT]"]
  R6 = Resistor [tolerance=±5% resistance=10k package=THT]

nets:
  N1: M1.pin_1, D2.anode, D4.cathode, Q4.C, Q3.C
  N2: M1.pin_2, D1.anode, D3.cathode, Q2.C, Q1.C
  5V: D1.cathode, D2.cathode, S1.Pin_3, S1.Pin_4, S2.Pin_3, S2.Pin_4, Q1.E, Q3.E
  GND: D3.anode, D4.anode, Q2.E, Q4.E, Q5.E, Q6.E
  N3: Q2.B, R2.Pin_1
  N4: Q4.B, R4.Pin_0
  CW: S1.Pin_1, S1.Pin_2, R4.Pin_1, R5.Pin_1
  CCW: S2.Pin_1, S2.Pin_2, R2.Pin_0, R6.Pin_1
  N5: R1.Pin_0, Q5.C
  N6: R1.Pin_1, Q1.B
  N7: R3.Pin_0, Q3.B
  N8: R3.Pin_1, Q6.C
  N9: Q5.B, R5.Pin_0
  N10: Q6.B, R6.Pin_0
