# Fritzing sketch circuit_1-1 (saved by Fritzing 0.8.7b)
breadboards: 1

parts:
  R2 = Resistor [tolerance=±5% resistance=1k package=THT]
  VCC1 = 4 x AAA Battery Mount

nets:
  N1: R2.Pin_0, VCC1.+
  N2: R2.Pin_1, VCC1.-
