# Fritzing sketch circuit_1-3 (saved by Fritzing 0.8.7b)
breadboards: 1

parts:
  R2 = Resistor [tolerance=±5% resistance=1k package=THT]
  R3 = Resistor [tolerance=±5% resistance=100 package=THT]
  VCC1 = 4 x AAA Battery Mount

nets:
  N1: R2.Pin_0, VCC1.+
  N2: R2.Pin_1, R3.Pin_0
  N3: R3.Pin_1, VCC1.-

custom parts:
  4 x AAA Battery Mount: A 4 x AAA battery pack (4.8 Volts with recharables)
