# Fritzing sketch circuit_1-7 (saved by Fritzing 0.8.7b)
breadboards: 1

parts:
  R2 = Resistor [tolerance=±5% resistance=1M package=THT]
  VCC1 = 4 x AAA Battery Mount
  S1 = Pushbutton [package="[THT]"]
  C1 = Ceramic Capacitor [capacitance=100nF package="100 mil [THT, multilayer]"]
  C2 = Ceramic Capacitor [capacitance=100nF package="100 mil [THT, multilayer]"]
  C3 = Ceramic Capacitor [capacitance=100nF package="100 mil [THT, multilayer]"]
  R3 = Resistor [tolerance=±5% resistance=1M package=THT]
  R4 = Resistor [tolerance=±5% resistance=1M package=THT]
  S2 = Pushbutton [package="[THT]"]
  R5 = Resistor [tolerance=±5% resistance=1M package=THT]

nets:
  N1: R2.Pin_0, S1.Pin_1, S1.Pin_2
  N2: R2.Pin_1, R4.Pin_0
  N3: VCC1.-, C1.0, C2.0, C3.0, R5.Pin_0
  N4: VCC1.+, S1.Pin_3, S1.Pin_4
  N5: C1.1, C2.1, C3.1, R3.Pin_1, S2.Pin_1, S2.Pin_2, S2.Pin_3, S2.Pin_4, R5.Pin_1
  N6: R3.Pin_0, R4.Pin_1

custom parts:
  4 x AAA Battery Mount: A 4 x AAA battery pack (4.8 Volts with recharables)
