# Fritzing sketch circuit_1-5 (saved by Fritzing 0.8.7b)
breadboards: 1

parts:
  R2 = Resistor [tolerance=±5% resistance=1M package=THT]
  VCC1 = 4 x AAA Battery Mount
  S1 = Pushbutton [package="[THT]"]
  C1 = Ceramic Capacitor [capacitance=100nF package="100 mil [THT, multilayer]"]

nets:
  N1: R2.Pin_0, S1.Pin_1, S1.Pin_2
  N2: R2.Pin_1, C1.1
  N3: VCC1.-, C1.0
  N4: VCC1.+, S1.Pin_3, S1.Pin_4

custom parts:
  4 x AAA Battery Mount: A 4 x AAA battery pack (4.8 Volts with recharables)
