# Fritzing sketch circuit_2-1-a (saved by Fritzing 0.8.7b)
breadboards: 1

parts:
  D1 = Rectifier Diode [part_number=1N4001 package="300 mil [THT]"]
  R1 = Resistor [tolerance=±5% resistance=1k package=THT]
  Ammeter = Amperemeter

nets:
  N1: D1.cathode, Ammeter.Positive
  N2: D1.anode, R1.Pin_1
  5V: R1.Pin_0
  GND: Ammeter.Com

custom parts:
  Amperemeter: A Standard Multimeter in Current mode
