# Fritzing sketch circuit_2-2-a (saved by Fritzing 0.8.7b)
breadboards: 1

parts:
  D1 = Rectifier Diode [part_number=1N4001 package="300 mil [THT]"]
  R1 = Resistor [tolerance=±5% resistance=3.3k package=THT]
  Voltmeter = Voltmeter

nets:
  GND: D1.cathode, Voltmeter.Com
  N1: D1.anode, R1.Pin_1, Voltmeter.Positive
  5V: R1.Pin_0

custom parts:
  Voltmeter: A Standard Multimeter in Current mode
