# Fritzing sketch circuit_2-3 (saved by Fritzing 0.8.7b)
breadboards: 1

parts:
  R1 = Resistor [tolerance=±5% resistance=330 package=THT]
  LED1 = LED - 3mm [color="Red (633nm)" package="3 mm [THT]"]
  S1 = Pushbutton [package="[THT]"]

nets:
  5V: R1.Pin_0
  N1: R1.Pin_1, LED1.anode
  N2: LED1.cathode, S1.Pin_3, S1.Pin_4
  GND: S1.Pin_1, S1.Pin_2
