# Fritzing sketch circuit_2-4 (saved by Fritzing 0.8.7b)
breadboards: 1

parts:
  R2 = Resistor [tolerance=±5% resistance=10k package=THT]
  S1 = Pushbutton [package="[THT]"]
  C1 = Ceramic Capacitor [capacitance=100nF package="100 mil [THT, multilayer]"]
  V1 = DC Power [voltage=5]
  Voltmeter1 = Voltmeter

nets:
  N1: R2.Pin_0, S1.Pin_1, S1.Pin_2
  N2: R2.Pin_1, C1.1, Voltmeter1.Positive
  N3: S1.Pin_3, S1.Pin_4, V1.V+
  N4: C1.0, V1.V-, Voltmeter1.Com

custom parts:
  Voltmeter: A Standard Multimeter in Current mode
