# Fritzing sketch circuit_2-5 (saved by Fritzing 0.8.7b)
breadboards: 1

parts:
  R1 = Resistor [tolerance=±5% resistance=10k package=THT]
  S1 = Pushbutton [package="[THT]"]
  C1 = Ceramic Capacitor [capacitance=100nF package="100 mil [THT, multilayer]"]
  V1 = DC Power [voltage=5]
  R2 = Resistor [tolerance=±5% resistance=330 package=THT]
  LED1 = LED - 3mm [color="Red (633nm)" package="3 mm [THT]"]
  S2 = Pushbutton [package="[THT]"]

nets:
  N1: R1.Pin_0, S1.Pin_1, S1.Pin_2
  N2: R1.Pin_1, C1.1, R2.Pin_0
  N3: S1.Pin_3, S1.Pin_4, V1.V+
  N4: C1.0, V1.V-, S2.Pin_3, S2.Pin_4
  N5: R2.Pin_1, LED1.anode
  N6: LED1.cathode, S2.Pin_1, S2.Pin_2

notes:
  discharge
  charge
