# Fritzing sketch 3-1b_voltage-divider (saved by Fritzing 0.8.7b)
breadboards: 1

parts:
  Voltmeter1 = Voltmeter
  R1 = Resistor [tolerance=±5% resistance=3.3 package=THT]
  R2 = Resistor [tolerance=±5% resistance=10k package=THT]

nets:
  N1: Voltmeter1.Positive, R1.Pin_1, R2.Pin_0
  GND: Voltmeter1.Com, R2.Pin_1
  5V: R1.Pin_0

custom parts:
  Voltmeter: A Standard Multimeter in Current mode
