# Fritzing sketch 3-2_potentiometer (saved by Fritzing 0.8.7b)
breadboards: 1

parts:
  Voltmeter1 = Voltmeter
  R1 = Rotary Potentiometer (Small) [maximum_resistance=100kΩ package=THT]

nets (from the schematic view):
  N1: Voltmeter1.Positive, R1.wiper
  GND: Voltmeter1.Com, R1.leg1
  5V: R1.leg2

custom parts:
  Voltmeter: A Standard Multimeter in Current mode
