# Fritzing sketch 3-3_rheostat (saved by Fritzing 0.8.7b)
breadboards: 1

parts:
  R1 = Rotary Potentiometer (Small) [maximum_resistance=100kΩ package=THT]
  Ohmmeter1 = Ohmmeter

nets:
  N1: R1.wiper, Ohmmeter1.Com
  N2: R1.leg2, Ohmmeter1.Positive

custom parts:
  Ohmmeter: A Standard Multimeter in Current mode
