# Fritzing sketch tr_2 (saved by Fritzing 0.8.7b)
breadboards: 1

parts:
  R_LED = Resistor [tolerance=±5% resistance=100 package=THT]
  Q1 = NPN-Transistor [part_number=2N3904 package="TO92 [THT]"]
  LED1 = LED - 3mm [color="Red (660nm)" package="3 mm [THT]"]
  R1 = Resistor [tolerance=±5% resistance=10k package=THT]
  S1 = Pushbutton [package="[THT]"]
  R2 = Resistor [tolerance=±5% resistance=100k package=THT]

nets:
  5V: R_LED.Pin_0, S1.Pin_3, S1.Pin_4
  N1: R_LED.Pin_1, LED1.anode
  GND: Q1.E, R2.Pin_1
  N2: Q1.B, R1.Pin_1, R2.Pin_0
  N3: Q1.C, LED1.cathode
  N4: R1.Pin_0, S1.Pin_1, S1.Pin_2
